// Logisim project FINALCircuit.circ as structural Verilog: 19 circuits, main circuit main
module main (
  input  NOTused,
  input  NOTused2,
  input  NOTused3
);

  wire and_1_out, and_2_out, clock_1_out, cu1_1_decoe, cu1_1_irwe, cu1_1_mar1we, cu1_1_mar2we, cu1_1_oprwe,
       cu1_1_pcoe, cu1_1_pcwe, cu1_1_ramoe, cu2_1_awe, cu2_1_bwe, cu2_1_flagwe, cu2_1_mar1oe, cu2_1_mar2oe,
       cu2_1_outoe, cu2_1_outwe, cu2_1_ramoe, cu3_1_awe, cu3_1_boe, cu3_1_bwe, cu3_1_mar1oe, cu3_1_ramoe,
       cu3_1_ramwe, cu3_1_reset, not_1_out, not_2_out, or_1_out, or_2_out, or_3_out, or_4_out, or_5_out;
  wire [3:0] extendedalu_1_flagstored, MAR1_stored, MAR2_stored, OPR_stored, pc_1_dataout, pc_1_stored,
       stepcounter_1_stored, undriven;
  wire [3:1] undriven_2;
  wire [3:2] IR_dataout;
  wire [7:0] extendedalu_1_aout, extendedalu_1_astored, extendedalu_1_bstored, extendedalu_1_stored,
       IR_stored, ram_1_dout;
  wire [7:4] IR_dataout_2;

  pc pc_1 (
    .WE(cu1_1_pcwe), .clock(clock_1_out), .OE(cu1_1_pcoe), .DATAOUT(pc_1_dataout), .STORED(pc_1_stored));  // open: MODE, value
  // Probe on pc_1_stored
  // Probe on extendedalu_1_astored
  EXTENDEDALU extendedalu_1 (
    .A(extendedalu_1_aout), .AWE(or_5_out), .AOE(NOTused3), .OE(cu2_1_outoe), .OUTWRITE(cu2_1_outwe),
    .B(extendedalu_1_aout), .BWE(or_4_out), .BOE(cu3_1_boe), .CLOCK(clock_1_out), .FlagOE(NOTused2),
    .FlagWE(cu2_1_flagwe), .S1(OPR_stored[0]), .S2(OPR_stored[1]), .S3(OPR_stored[2]), .S4(OPR_stored[3]),
    .ASTORED(extendedalu_1_astored), .AOUT(extendedalu_1_aout), .BSTORED(extendedalu_1_bstored),
    .BOUT(extendedalu_1_aout), .STORED(extendedalu_1_stored), .DATAOUT(extendedalu_1_aout),
    .FlagStored(extendedalu_1_flagstored));  // open: FlagOUT
  // Probe on extendedalu_1_bstored
  // Probe on extendedalu_1_stored
  // Probe on extendedalu_1_flagstored
  RAM #(.addrWidth(4), .asyncread("true")) ram_1 (
    .addr(pc_1_dataout), .we(cu3_1_ramwe), .oe(or_2_out), .clk(clock_1_out), .din(extendedalu_1_aout),
    .dout(ram_1_dout));
  not not_1 (not_1_out, and_1_out);
  and and_1 (and_1_out, or_5_out, cu3_1_boe);
  Clock clock_1 (.out(clock_1_out));
  or or_1 (or_1_out, or_5_out, or_4_out, cu1_1_irwe);
  not not_2 (not_2_out, cu2_1_outoe);
  // Probe on stepcounter_1_stored
  stepcounter stepcounter_1 (
    .value(undriven), .clock(clock_1_out), .Reset(cu3_1_reset), .STORED(stepcounter_1_stored));  // open: MODE
  // Probe on ram_1_dout
  assign extendedalu_1_aout = and_2_out ? ram_1_dout : 8'bz;  // Controlled_Buffer controlled_buffer_1
  and and_2 (and_2_out, or_1_out, not_1_out, not_2_out);
  CU1 cu1_1 (
    .stepcounter(stepcounter_1_stored), .PCOE(cu1_1_pcoe), .RAMOE(cu1_1_ramoe), .IRWE(cu1_1_irwe),
    .PCWE(cu1_1_pcwe), .DECOE(cu1_1_decoe), .MAR1WE(cu1_1_mar1we), .MAR2WE(cu1_1_mar2we), .OPRWE(cu1_1_oprwe));
  // Probe on IR_stored
  EightBItRegistar IR (
    .Datain(extendedalu_1_aout), .WE(cu1_1_irwe), .Clock(clock_1_out), .OE(cu1_1_decoe), .stored(IR_stored),
    .Dataout({IR_dataout_2, IR_dataout, undriven_2[3:2]}));  // open: Reset
  // Probe on MAR1_stored
  FourBitRegistar MAR1 (
    .Datain({undriven_2, 1'b1}), .WE(cu1_1_mar1we), .Clock(clock_1_out), .OE(or_3_out), .Stored(MAR1_stored),
    .Dataout(pc_1_dataout));  // open: Reset
  // Probe on MAR2_stored
  FourBitRegistar MAR2 (
    .Datain({IR_dataout, 2'b11}), .WE(cu1_1_mar2we), .Clock(clock_1_out), .OE(cu2_1_mar2oe),
    .Stored(MAR2_stored), .Dataout(pc_1_dataout));  // open: Reset
  or or_2 (or_2_out, cu1_1_ramoe, cu3_1_ramoe, cu2_1_ramoe);
  // Probe on OPR_stored
  FourBitRegistar OPR (
    .Datain(IR_dataout_2), .WE(cu1_1_oprwe), .Clock(clock_1_out), .OE(NOTused), .Stored(OPR_stored));  // open: Reset, Dataout
  CU2 cu2_1 (
    .OPCODE(OPR_stored), .STEPCOUNTER(stepcounter_1_stored), .MAR1OE(cu2_1_mar1oe), .RAMOE(cu2_1_ramoe),
    .AWE(cu2_1_awe), .MAR2OE(cu2_1_mar2oe), .BWE(cu2_1_bwe), .OUTWE(cu2_1_outwe), .FLAGWE(cu2_1_flagwe),
    .OUTOE(cu2_1_outoe));
  CU3 cu3_1 (
    .opcode(OPR_stored), .stepcounter(stepcounter_1_stored), .MAR1OE(cu3_1_mar1oe), .RAMOE(cu3_1_ramoe),
    .BWE(cu3_1_bwe), .BOE(cu3_1_boe), .RAMWE(cu3_1_ramwe), .AWE(cu3_1_awe), .RESET(cu3_1_reset));
  or or_3 (or_3_out, cu2_1_mar1oe, cu3_1_mar1oe);
  or or_4 (or_4_out, cu2_1_bwe, cu3_1_bwe);
  or or_5 (or_5_out, cu2_1_awe, cu3_1_awe);

  // Notes on the sheet:
  //   DATA BUS
  //   DATA BUS
  //   ADDRESS BUS
  //   DATA BUS
  //   ADDRESS BUS
endmodule

module TwoBitAdder (
  input  A,
  input  B,
  input  Carry_IN,
  output Sum,
  output Carry_OUT
);

  wire and_1_out, and_2_out, xor_1_out;

  xor xor_1 (xor_1_out, A, B);
  and and_1 (and_1_out, A, B);
  xor xor_2 (Sum, xor_1_out, Carry_IN);
  and and_2 (and_2_out, xor_1_out, Carry_IN);
  or or_1 (Carry_OUT, and_1_out, and_2_out);
endmodule

module pc (
  input  MODE,
  input  [3:0] value,
  input  WE,
  input  clock,
  input  OE,
  output [3:0] DATAOUT,
  output [3:0] STORED
);

  wire and_1_out;
  wire [3:0] fourbitadder_1_sum, fourbitmux_1_choice, xnor_1_out;

  Register #(.width(4)) register_1 (.D(fourbitmux_1_choice), .en(WE), .clk(clock), .Q(STORED), .clr(and_1_out));
  FourBitMux fourbitmux_1 (.S1(MODE), .IN1(fourbitadder_1_sum), .IN2(value), .CHOICE(fourbitmux_1_choice));
  and and_1 (and_1_out, xnor_1_out[0], xnor_1_out[1], xnor_1_out[2], xnor_1_out[3]);
  assign xnor_1_out = ~(STORED ^ 4'b1111);  // XNOR_Gate xnor_1, 4 bits wide
  FourBitAdder fourbitadder_1 (.A(STORED), .B(4'b0010), .sum(fourbitadder_1_sum));  // open: sub, overflow
  assign DATAOUT = OE ? STORED : 4'bz;  // Controlled_Buffer controlled_buffer_1
endmodule

module FourBitAdder (
  input  [3:0] A,
  input  sub,
  input  [3:0] B,
  output [3:0] sum,
  output overflow
);

  wire not_1_out, twobitadder_1_carry_out, twobitadder_2_carry_out, twobitadder_3_carry_out,
       twobitadder_4_carry_out;
  wire [3:0] bit_extender_1_out, xor_1_out;

  // Probe on B
  // Probe on bit_extender_1_out
  // Probe on A
  assign bit_extender_1_out = {{3{sub}}, sub};  // Bit_Extender bit_extender_1
  assign xor_1_out = B ^ bit_extender_1_out;  // XOR_Gate xor_1, 4 bits wide
  TwoBitAdder twobitadder_1 (
    .A(A[0]), .B(xor_1_out[0]), .Carry_IN(sub), .Sum(sum[0]), .Carry_OUT(twobitadder_1_carry_out));
  TwoBitAdder twobitadder_2 (
    .A(A[1]), .B(xor_1_out[1]), .Carry_IN(twobitadder_1_carry_out), .Sum(sum[1]),
    .Carry_OUT(twobitadder_2_carry_out));
  TwoBitAdder twobitadder_3 (
    .A(A[2]), .B(xor_1_out[2]), .Carry_IN(twobitadder_2_carry_out), .Sum(sum[2]),
    .Carry_OUT(twobitadder_3_carry_out));
  TwoBitAdder twobitadder_4 (
    .A(A[3]), .B(xor_1_out[3]), .Carry_IN(twobitadder_3_carry_out), .Sum(sum[3]),
    .Carry_OUT(twobitadder_4_carry_out));
  not not_1 (not_1_out, sub);
  and and_1 (overflow, twobitadder_4_carry_out, not_1_out);
  // Probe on sum
endmodule

module FourBitMux (
  input  S1,
  input  [3:0] IN1,
  input  [3:0] IN2,
  output [3:0] CHOICE
);

  wire [3:0] and_1_out, and_2_out, bit_extender_1_out, not_1_out;

  assign bit_extender_1_out = {{3{S1}}, S1};  // Bit_Extender bit_extender_1
  // Probe on bit_extender_1_out
  // Probe on bit_extender_1_out
  // Probe on not_1_out
  assign not_1_out = ~bit_extender_1_out;  // NOT_Gate not_1, 4 bits wide
  assign and_1_out = not_1_out & IN1;  // AND_Gate and_1, 4 bits wide
  assign and_2_out = IN2 & bit_extender_1_out;  // AND_Gate and_2, 4 bits wide
  // Probe on and_1_out
  // Probe on and_2_out
  assign CHOICE = and_1_out | and_2_out;  // OR_Gate or_1, 4 bits wide
endmodule

module ALU (
  input  [3:0] A,
  input  AWE,
  input  OE,
  input  [3:0] B,
  input  OUTWRITE,
  input  BWE,
  input  S1,
  input  S2,
  input  CLOCK,
  output [3:0] ASTORED,
  output [3:0] STORED,
  output [3:0] DATAOUT,
  output [3:0] BSTORED
);

  wire [3:0] and_1_out, fourbitadder_1_sum, fourbitmux_1_choice, fourbitmux_2_choice, or_1_out;

  Register #(.width(4)) register_1 (.D(A), .en(AWE), .clk(CLOCK), .Q(ASTORED));  // open: clr
  Register #(.width(4)) register_2 (.D(B), .en(BWE), .clk(CLOCK), .Q(BSTORED));  // open: clr
  assign and_1_out = ASTORED & BSTORED;  // AND_Gate and_1, 4 bits wide
  assign or_1_out = ASTORED | BSTORED;  // OR_Gate or_1, 4 bits wide
  FourBitAdder fourbitadder_1 (.A(ASTORED), .sub(S1), .B(BSTORED), .sum(fourbitadder_1_sum));  // open: overflow
  FourBitMux fourbitmux_1 (.S1(S1), .IN1(and_1_out), .IN2(or_1_out), .CHOICE(fourbitmux_1_choice));
  FourBitMux fourbitmux_2 (.S1(S2), .IN1(fourbitmux_1_choice), .IN2(fourbitadder_1_sum), .CHOICE(fourbitmux_2_choice));
  Register #(.width(4)) register_3 (.D(fourbitmux_2_choice), .en(OUTWRITE), .clk(CLOCK), .Q(STORED));  // open: clr
  assign DATAOUT = OE ? STORED : 4'bz;  // Controlled_Buffer controlled_buffer_1
endmodule

module EightBItRegistar (
  input  [7:0] Datain,
  input  WE,
  input  Clock,
  input  Reset,
  input  OE,
  output [7:0] stored,
  output [7:0] Dataout
);

  Register register_1 (.D(Datain), .en(WE), .clk(Clock), .Q(stored), .clr(Reset));
  assign Dataout = OE ? stored : 8'bz;  // Controlled_Buffer controlled_buffer_1
endmodule

module FourBitRegistar (
  input  [3:0] Datain,
  input  WE,
  input  Clock,
  input  Reset,
  input  OE,
  output [3:0] Stored,
  output [3:0] Dataout
);

  Register #(.width(4)) register_1 (.D(Datain), .en(WE), .clk(Clock), .Q(Stored), .clr(Reset));
  assign Dataout = OE ? Stored : 4'bz;  // Controlled_Buffer controlled_buffer_1
endmodule

module stepcounter (
  input  MODE,
  input  [3:0] value,
  input  clock,
  input  Reset,
  output [3:0] STORED
);

  wire and_1_out, or_1_out;
  wire [3:0] fourbitadder_1_sum, fourbitmux_1_choice, xnor_1_out;

  or or_1 (or_1_out, Reset, and_1_out);
  Register #(.width(4)) register_1 (.D(fourbitmux_1_choice), .en(clock), .clk(clock), .Q(STORED), .clr(or_1_out));
  FourBitMux fourbitmux_1 (.S1(MODE), .IN1(fourbitadder_1_sum), .IN2(value), .CHOICE(fourbitmux_1_choice));
  and and_1 (and_1_out, xnor_1_out[0], xnor_1_out[1], xnor_1_out[2], xnor_1_out[3]);
  assign xnor_1_out = ~(STORED ^ 4'b1010);  // XNOR_Gate xnor_1, 4 bits wide
  FourBitAdder fourbitadder_1 (.A(STORED), .B(4'b0001), .sum(fourbitadder_1_sum));  // open: sub, overflow
endmodule

module CU1 (
  input  [3:0] stepcounter,
  output PCOE,
  output RAMOE,
  output IRWE,
  output PCWE,
  output DECOE,
  output MAR1WE,
  output MAR2WE,
  output OPRWE
);

  wire not_1_out, not_2_out, not_3_out, not_4_out;

  not not_1 (not_1_out, stepcounter[3]);
  not not_2 (not_2_out, stepcounter[2]);
  not not_3 (not_3_out, stepcounter[1]);
  not not_4 (not_4_out, stepcounter[0]);
  and and_1 (PCOE, not_1_out, not_2_out, not_3_out, stepcounter[0]);
  and and_2 (RAMOE, not_1_out, not_2_out, not_3_out, stepcounter[0]);
  and and_3 (IRWE, not_1_out, not_2_out, stepcounter[1], not_4_out);
  and and_4 (PCWE, not_1_out, not_2_out, stepcounter[1], not_4_out);
  and and_5 (DECOE, not_1_out, not_2_out, stepcounter[1], stepcounter[0]);
  and and_6 (MAR1WE, not_1_out, not_2_out, stepcounter[1], stepcounter[0]);
  and and_7 (MAR2WE, not_1_out, not_2_out, stepcounter[1], stepcounter[0]);
  and and_8 (OPRWE, not_1_out, not_2_out, stepcounter[1], stepcounter[0]);
endmodule

module temp (
  input  S1,
  input  in_2,
  input  [3:0] in_3,
  input  IN1,
  input  IN2,
  input  in_6,
  input  CLK,
  input  DECWE,
  input  IROE,
  input  MAR1OE,
  input  DECOE,
  input  IRWE,
  input  in_13,
  input  PCOE,
  input  MAR1WE,
  input  in_16,
  input  PCWE,
  input  MAR2OE,
  input  MAR2WE,
  input  RAMWE,
  input  RAMOE,
  input  in_22,
  input  [3:0] in_23,
  input  switchfortwoscompliment,
  input  AWE,
  input  in_26,
  input  AOE,
  input  in_28,
  input  in_29,
  input  BWE,
  input  [3:0] in_31,
  input  S2,
  input  in_33,
  input  BOE,
  input  clock,
  input  MOE,
  input  [3:0] Manualin,
  output CHOICE,
  output [3:0] out_39,
  output negativeoverflow,
  output positiveoverflow
);

  wire and_1_out, and_2_out, not_1_out, or_2_out, twobitadder_1_carry_out, twobitadder_2_carry_out,
       twobitadder_3_carry_out, twobitadder_4_carry_out, twobitadder_5_carry_out, twobitadder_6_carry_out,
       twobitadder_7_carry_out, twobitadder_8_carry_out, xor_2_out, xor_3_out, xor_4_out, xor_5_out,
       xor_6_out, xor_7_out;
  wire [3:0] A_dataout, A_stored, alu_1_astored, alu_1_bstored, alu_1_stored, and_6_out, B_stored,
       bit_extender_1_out, bit_extender_2_out, IR_stored, MAR1_stored, MAR2_stored, pc_1_dataout,
       pc_1_stored, register_1_q, register_2_q, register_3_q, twobitadder_1_sum, xor_1_out;
  wire [3:1] undriven;
  wire [3:2] DECODER_dataout;
  wire [4:4] and_5_out;
  wire [7:0] DECODER_stored, ram_1_dout, WRITEBACK_dataout, WRITEBACK_stored;
  wire [7:4] DECODER_dataout_2;

  Register #(.width(4)) register_1 (.Q(register_1_q));  // open: D, en, clk, clr
  // Probe on bit_extender_1_out
  // Probe on register_1_q
  // Probe on register_2_q
  Register #(.width(4)) register_2 (.Q(register_2_q));  // open: D, en, clk, clr
  assign bit_extender_1_out = {{3{in_6}}, in_6};  // Bit_Extender bit_extender_1
  assign xor_1_out = register_1_q ^ bit_extender_1_out;  // XOR_Gate xor_1, 4 bits wide
  xor xor_2 (xor_2_out, in_31[3], switchfortwoscompliment);
  not not_1 (not_1_out, S1);
  and and_1 (and_1_out, not_1_out, IN1);
  xor xor_3 (xor_3_out, in_31[2], switchfortwoscompliment);
  and and_2 (and_2_out, IN2, S1);
  xor xor_4 (xor_4_out, in_31[1], switchfortwoscompliment);
  xor xor_5 (xor_5_out, in_31[0], switchfortwoscompliment);
  or or_1 (CHOICE, and_1_out, and_2_out);
  TwoBitAdder twobitadder_1 (
    .A(register_2_q[0]), .B(xor_1_out[0]), .Carry_IN(in_6), .Sum(twobitadder_1_sum[0]),
    .Carry_OUT(twobitadder_1_carry_out));
  TwoBitAdder twobitadder_2 (
    .A(register_2_q[1]), .B(xor_1_out[1]), .Carry_IN(twobitadder_1_carry_out), .Sum(twobitadder_1_sum[1]),
    .Carry_OUT(twobitadder_2_carry_out));
  TwoBitAdder twobitadder_3 (
    .A(register_2_q[2]), .B(xor_1_out[2]), .Carry_IN(twobitadder_2_carry_out), .Sum(twobitadder_1_sum[2]),
    .Carry_OUT(twobitadder_3_carry_out));
  TwoBitAdder twobitadder_4 (
    .A(register_2_q[3]), .B(xor_1_out[3]), .Carry_IN(twobitadder_3_carry_out), .Sum(twobitadder_1_sum[3]),
    .Carry_OUT(twobitadder_4_carry_out));
  TwoBitAdder twobitadder_5 (
    .A(in_23[0]), .B(xor_5_out), .Carry_IN(switchfortwoscompliment), .Sum(out_39[0]),
    .Carry_OUT(twobitadder_5_carry_out));
  TwoBitAdder twobitadder_6 (
    .A(in_23[1]), .B(xor_4_out), .Carry_IN(twobitadder_5_carry_out), .Sum(out_39[1]),
    .Carry_OUT(twobitadder_6_carry_out));
  TwoBitAdder twobitadder_7 (
    .A(in_23[2]), .B(xor_3_out), .Carry_IN(twobitadder_6_carry_out), .Sum(out_39[2]),
    .Carry_OUT(twobitadder_7_carry_out));
  TwoBitAdder twobitadder_8 (
    .A(in_23[3]), .B(xor_2_out), .Carry_IN(twobitadder_7_carry_out), .Sum(out_39[3]),
    .Carry_OUT(twobitadder_8_carry_out));
  xor xor_6 (xor_6_out, twobitadder_4_carry_out, twobitadder_3_carry_out);
  and and_3 (negativeoverflow, twobitadder_8_carry_out, xor_7_out);
  xor xor_7 (xor_7_out, twobitadder_8_carry_out, twobitadder_7_carry_out);
  and and_4 (positiveoverflow, xor_7_out, twobitadder_7_carry_out);
  assign bit_extender_2_out = {{3{xor_6_out}}, xor_6_out};  // Bit_Extender bit_extender_2
  and and_5 (and_5_out[4], xor_6_out, twobitadder_4_carry_out);
  Register #(.width(4)) register_3 (.D(twobitadder_1_sum), .clk(in_22), .Q(register_3_q));  // open: en, clr
  // Probe on twobitadder_1_sum
  assign and_6_out = bit_extender_2_out & register_3_q;  // AND_Gate and_6, 4 bits wide
  // Probe on {and_5_out[4], and_6_out}
  Register #(.width(5)) overflowregister (.D({and_5_out[4], and_6_out}), .clk(in_22));  // open: en, Q, clr
  // Probe on A_stored
  FourBitRegistar A (
    .Datain(A_dataout), .WE(AWE), .Clock(clock), .OE(AOE), .Stored(A_stored), .Dataout(A_dataout));  // open: Reset
  FourBitRegistar B (
    .Datain(A_dataout), .WE(BWE), .Clock(clock), .OE(BOE), .Stored(B_stored), .Dataout(A_dataout));  // open: Reset
  pc pc_1 (.MODE(in_2), .value(in_3), .WE(PCWE), .clock(CLK), .OE(PCOE), .DATAOUT(pc_1_dataout), .STORED(pc_1_stored));
  // Probe on WRITEBACK_stored
  EightBItRegistar WRITEBACK (
    .Datain(WRITEBACK_dataout), .WE(in_16), .Clock(CLK), .OE(in_13), .stored(WRITEBACK_stored),
    .Dataout(WRITEBACK_dataout));  // open: Reset
  // Probe on B_stored
  // Probe on pc_1_stored
  assign A_dataout = MOE ? Manualin : 4'bz;  // Controlled_Buffer controlled_buffer_1
  RAM #(.addrWidth(4)) ram_1 (
    .addr(pc_1_dataout), .we(RAMWE), .oe(RAMOE), .clk(CLK), .din(WRITEBACK_dataout), .dout(ram_1_dout));
  or or_2 (or_2_out, in_16, DECWE);
  // Probe on ram_1_dout
  assign WRITEBACK_dataout = or_2_out ? ram_1_dout : 8'bz;  // Controlled_Buffer controlled_buffer_2
  ALU alu_1 (
    .A(A_dataout), .AWE(in_26), .B(A_dataout), .OUTWRITE(in_28), .BWE(in_29), .S1(in_33), .S2(S2),
    .CLOCK(clock), .ASTORED(alu_1_astored), .STORED(alu_1_stored), .BSTORED(alu_1_bstored));  // open: OE, DATAOUT
  // Probe on alu_1_astored
  // Probe on alu_1_stored
  // Probe on alu_1_bstored
  // Probe on DECODER_stored
  EightBItRegistar DECODER (
    .Datain(WRITEBACK_dataout), .WE(DECWE), .Clock(CLK), .OE(DECOE), .stored(DECODER_stored),
    .Dataout({DECODER_dataout_2, DECODER_dataout, undriven[3:2]}));  // open: Reset
  // Probe on nothing
  // Probe on MAR1_stored
  FourBitRegistar MAR1 (
    .Datain({undriven, 1'b1}), .WE(MAR1WE), .Clock(CLK), .OE(MAR1OE), .Stored(MAR1_stored),
    .Dataout(pc_1_dataout));  // open: Reset
  // Probe on MAR2_stored
  FourBitRegistar MAR2 (
    .Datain({DECODER_dataout, 2'b11}), .WE(MAR2WE), .Clock(CLK), .OE(MAR2OE), .Stored(MAR2_stored),
    .Dataout(pc_1_dataout));  // open: Reset
  // Probe on IR_stored
  FourBitRegistar IR (
    .Datain(DECODER_dataout_2), .WE(IRWE), .Clock(CLK), .OE(IROE), .Stored(IR_stored));  // open: Reset, Dataout

  // Notes on the sheet:
  //   DATA BUS
  //   DATA BUS
  //   ADDRESS BUS
  //   DATA BUS
  //   ADDRESS BUS
endmodule

module EXTENDEDALU (
  input  [7:0] A,
  input  AWE,
  input  AOE,
  input  OE,
  input  OUTWRITE,
  input  [7:0] B,
  input  BWE,
  input  BOE,
  input  CLOCK,
  input  FlagOE,
  input  FlagWE,
  input  S1,
  input  S2,
  input  S3,
  input  S4,
  output [7:0] ASTORED,
  output [7:0] AOUT,
  output [7:0] BSTORED,
  output [7:0] BOUT,
  output [7:0] STORED,
  output [7:0] DATAOUT,
  output [3:0] FlagStored,
  output [3:0] FlagOUT
);

  wire and_2_out, and_3_out, and_4_out, and_5_out, and_6_out, and_7_out, and_8_out,
       eightbitadder_1_negativeoverflow, eightbitadder_1_positiveoverflow, leftshifter_1_overflow,
       leftshifter_2_overflow, not_1_out, not_2_out, not_3_out, not_4_out, not_5_out, not_6_out, not_7_out,
       or_2_out, or_3_out, rightshifter_1_underflow, rightshifter_2_underflow;
  wire [3:0] and_9_out;
  wire [7:0] and_1_out, eightbitadder_1_out_4, eightbitcomparator_1_equal, eightbitcomparator_1_greater,
       eightbitcomparator_1_lesser, eightbitmux_1_choice, eightbitmux_2_choice, eightbitmux_3_choice,
       eightbitmux_4_choice, eightbitmux_5_choice, eightbitmux_6_choice, eightbitmux_7_choice,
       eightbitmux_8_choice, eightbitmux_9_choice, eightbitmux_10_choice, leftshifter_1_out_2,
       leftshifter_2_out_2, or_1_out, rightshifter_1_out_3, rightshifter_2_out_3, xor_1_out;

  Register register_1 (.D(A), .en(AWE), .clk(CLOCK), .Q(ASTORED));  // open: clr
  Register register_2 (.D(B), .en(BWE), .clk(CLOCK), .Q(BSTORED));  // open: clr
  assign and_1_out = ASTORED & BSTORED;  // AND_Gate and_1, 8 bits wide
  assign or_1_out = ASTORED | BSTORED;  // OR_Gate or_1, 8 bits wide
  assign xor_1_out = ASTORED ^ BSTORED;  // XOR_Gate xor_1, 8 bits wide
  EightBitComparator eightbitcomparator_1 (
    .A(ASTORED), .B(BSTORED), .Greater(eightbitcomparator_1_greater), .Equal(eightbitcomparator_1_equal),
    .Lesser(eightbitcomparator_1_lesser));
  LeftShifter leftshifter_1 (.in_1(ASTORED), .out_2(leftshifter_1_out_2), .Overflow(leftshifter_1_overflow));
  LeftShifter leftshifter_2 (.in_1(BSTORED), .out_2(leftshifter_2_out_2), .Overflow(leftshifter_2_overflow));
  RightShifter rightshifter_1 (.in_1(ASTORED), .Underflow(rightshifter_1_underflow), .out_3(rightshifter_1_out_3));
  RightShifter rightshifter_2 (.in_1(BSTORED), .Underflow(rightshifter_2_underflow), .out_3(rightshifter_2_out_3));
  EightBitAdder eightbitadder_1 (
    .A(ASTORED), .sub(S1), .B(BSTORED), .out_4(eightbitadder_1_out_4),
    .negativeoverflow(eightbitadder_1_negativeoverflow), .positiveoverflow(eightbitadder_1_positiveoverflow));
  EightBitMUX eightbitmux_1 (
    .S1(S1), .IN1(xor_1_out), .IN2(eightbitcomparator_1_greater), .CHOICE(eightbitmux_1_choice));
  EightBitMUX eightbitmux_2 (
    .S1(S1), .IN1(eightbitcomparator_1_equal), .IN2(eightbitcomparator_1_lesser),
    .CHOICE(eightbitmux_2_choice));
  EightBitMUX eightbitmux_3 (
    .S1(S1), .IN1(leftshifter_1_out_2), .IN2(leftshifter_2_out_2), .CHOICE(eightbitmux_3_choice));
  EightBitMUX eightbitmux_4 (
    .S1(S1), .IN1(rightshifter_1_out_3), .IN2(rightshifter_2_out_3), .CHOICE(eightbitmux_4_choice));
  EightBitMUX eightbitmux_5 (.S1(S1), .IN1(and_1_out), .IN2(or_1_out), .CHOICE(eightbitmux_5_choice));
  EightBitMUX eightbitmux_6 (
    .S1(S2), .IN1(eightbitmux_3_choice), .IN2(eightbitmux_4_choice), .CHOICE(eightbitmux_6_choice));
  EightBitMUX eightbitmux_7 (
    .S1(S2), .IN1(eightbitmux_1_choice), .IN2(eightbitmux_2_choice), .CHOICE(eightbitmux_7_choice));
  EightBitMUX eightbitmux_8 (
    .S1(S2), .IN1(eightbitmux_5_choice), .IN2(eightbitadder_1_out_4), .CHOICE(eightbitmux_8_choice));
  assign AOUT = AOE ? ASTORED : 8'bz;  // Controlled_Buffer controlled_buffer_1
  assign BOUT = BOE ? BSTORED : 8'bz;  // Controlled_Buffer controlled_buffer_2
  EightBitMUX eightbitmux_9 (
    .S1(S4), .IN1(eightbitmux_8_choice), .IN2(eightbitmux_7_choice), .CHOICE(eightbitmux_9_choice));
  not not_1 (not_1_out, S1);
  not not_2 (not_2_out, S2);
  not not_3 (not_3_out, S1);
  EightBitMUX eightbitmux_10 (
    .S1(S3), .IN1(eightbitmux_9_choice), .IN2(eightbitmux_6_choice), .CHOICE(eightbitmux_10_choice));
  and and_2 (and_2_out, not_1_out, not_2_out, S4, S3, leftshifter_1_overflow);
  and and_3 (and_3_out, leftshifter_2_overflow, S3, S4, not_4_out, S1);
  not not_4 (not_4_out, S2);
  and and_4 (and_4_out, S1, S2, S3, S4, rightshifter_2_underflow);
  and and_5 (and_5_out, rightshifter_1_underflow, S4, S3, S2, not_3_out);
  Register register_3 (.D(eightbitmux_10_choice), .en(OUTWRITE), .clk(CLOCK), .Q(STORED));  // open: clr
  or or_2 (or_2_out, and_2_out, and_3_out);
  or or_3 (or_3_out, and_4_out, and_5_out);
  assign DATAOUT = OE ? STORED : 8'bz;  // Controlled_Buffer controlled_buffer_3
  and and_6 (and_6_out, S4, S3, S2);
  and and_7 (and_7_out, S4, S3, not_5_out);
  not not_5 (not_5_out, S2);
  and and_8 (and_8_out, not_6_out, not_7_out);
  not not_6 (not_6_out, S4);
  not not_7 (not_7_out, S3);
  and and_9 (and_9_out[0], eightbitadder_1_negativeoverflow, and_8_out);
  and and_10 (and_9_out[1], eightbitadder_1_positiveoverflow, and_8_out);
  and and_11 (and_9_out[2], or_2_out, and_7_out);
  and and_12 (and_9_out[3], or_3_out, and_6_out);
  Register #(.width(4)) FlagRegister (.D(and_9_out), .en(FlagWE), .clk(CLOCK), .Q(FlagStored));  // open: clr
  assign FlagOUT = FlagOE ? FlagStored : 4'bz;  // Controlled_Buffer controlled_buffer_4
endmodule

module EightBitComparator (
  input  [7:0] A,
  input  [7:0] B,
  output [7:0] Greater,
  output [7:0] Equal,
  output [7:0] Lesser
);

  wire and_3_out, and_4_out, and_5_out, and_6_out, and_7_out, and_8_out, and_9_out, and_10_out, and_11_out,
       and_12_out, and_13_out, and_14_out, and_15_out, and_16_out, nor_2_out, or_1_out, or_2_out;
  wire [7:0] and_1_out, and_2_out, nor_1_out, not_1_out, not_2_out;

  assign not_1_out = ~B;  // NOT_Gate not_1, 8 bits wide
  assign not_2_out = ~A;  // NOT_Gate not_2, 8 bits wide
  assign and_1_out = A & not_1_out;  // AND_Gate and_1, 8 bits wide
  assign and_2_out = B & not_2_out;  // AND_Gate and_2, 8 bits wide
  assign nor_1_out = ~(and_1_out | and_2_out);  // NOR_Gate nor_1, 8 bits wide
  and and_3 (and_3_out, nor_1_out[7], and_1_out[6]);
  and and_4 (and_4_out, nor_1_out[7], and_2_out[6]);
  and and_5 (and_5_out, nor_1_out[5], nor_1_out[7], and_1_out[5]);
  and and_6 (and_6_out, nor_1_out[5], nor_1_out[7], and_2_out[5]);
  and and_7 (and_7_out, nor_1_out[5], nor_1_out[6], nor_1_out[7], and_1_out[4]);
  and and_8 (and_8_out, nor_1_out[5], nor_1_out[6], nor_1_out[7], and_2_out[4]);
  and and_9 (and_9_out, nor_1_out[4], nor_1_out[5], nor_1_out[6], nor_1_out[7], and_1_out[3]);
  and and_10 (and_10_out, nor_1_out[4], nor_1_out[5], nor_1_out[6], nor_1_out[7], and_2_out[3]);
  and and_11 (and_11_out, nor_1_out[3], nor_1_out[4], nor_1_out[5], nor_1_out[6], nor_1_out[7], and_1_out[2]);
  and and_12 (and_12_out, nor_1_out[3], nor_1_out[4], nor_1_out[5], nor_1_out[6], nor_1_out[7], and_2_out[2]);
  and and_13 (and_13_out, nor_1_out[2], nor_1_out[3], nor_1_out[4], nor_1_out[5], nor_1_out[6], nor_1_out[7], and_1_out[1]);
  and and_14 (and_14_out, nor_1_out[2], nor_1_out[3], nor_1_out[4], nor_1_out[5], nor_1_out[6], nor_1_out[7], and_2_out[1]);
  and and_15 (and_15_out, nor_1_out[1], nor_1_out[2], nor_1_out[3], nor_1_out[4], nor_1_out[5], nor_1_out[6], nor_1_out[7], and_1_out[0]);
  and and_16 (and_16_out, nor_1_out[1], nor_1_out[2], nor_1_out[3], nor_1_out[4], nor_1_out[5], nor_1_out[6], nor_1_out[7], and_2_out[0]);
  or or_1 (or_1_out, and_15_out, and_13_out, and_11_out, and_9_out, and_7_out, and_5_out, and_3_out, and_1_out[7]);
  or or_2 (or_2_out, and_16_out, and_14_out, and_12_out, and_10_out, and_8_out, and_6_out, and_4_out, and_2_out[7]);
  nor nor_2 (nor_2_out, or_1_out, or_2_out);
  assign Greater = {{7{1'b0}}, or_1_out};  // Bit_Extender bit_extender_1
  assign Lesser = {{7{1'b0}}, or_2_out};  // Bit_Extender bit_extender_2
  assign Equal = {{7{1'b0}}, nor_2_out};  // Bit_Extender bit_extender_3
endmodule

module EightBitMUX (
  input  S1,
  input  [7:0] IN1,
  input  [7:0] IN2,
  output [7:0] CHOICE
);

  wire [7:0] and_1_out, and_2_out, bit_extender_1_out, not_1_out;

  assign bit_extender_1_out = {{7{S1}}, S1};  // Bit_Extender bit_extender_1
  // Probe on bit_extender_1_out
  // Probe on bit_extender_1_out
  // Probe on not_1_out
  assign not_1_out = ~bit_extender_1_out;  // NOT_Gate not_1, 8 bits wide
  assign and_1_out = not_1_out & IN1;  // AND_Gate and_1, 8 bits wide
  assign and_2_out = IN2 & bit_extender_1_out;  // AND_Gate and_2, 8 bits wide
  // Probe on and_1_out
  // Probe on and_2_out
  assign CHOICE = and_1_out | and_2_out;  // OR_Gate or_1, 8 bits wide
endmodule

module EightBitAdder (
  input  [7:0] A,
  input  sub,
  input  [7:0] B,
  output [7:0] out_4,
  output negativeoverflow,
  output positiveoverflow
);

  wire twobitadder_1_carry_out, twobitadder_2_carry_out, twobitadder_3_carry_out, twobitadder_4_carry_out,
       twobitadder_5_carry_out, twobitadder_6_carry_out, twobitadder_7_carry_out, twobitadder_8_carry_out,
       xor_2_out;
  wire [7:0] bit_extender_1_out, xor_1_out;

  assign bit_extender_1_out = {{7{sub}}, sub};  // Bit_Extender bit_extender_1
  assign xor_1_out = bit_extender_1_out ^ B;  // XOR_Gate xor_1, 8 bits wide
  TwoBitAdder twobitadder_1 (
    .A(A[0]), .B(xor_1_out[0]), .Carry_IN(sub), .Sum(out_4[0]), .Carry_OUT(twobitadder_1_carry_out));
  TwoBitAdder twobitadder_2 (
    .A(A[1]), .B(xor_1_out[1]), .Carry_IN(twobitadder_1_carry_out), .Sum(out_4[1]),
    .Carry_OUT(twobitadder_2_carry_out));
  TwoBitAdder twobitadder_3 (
    .A(A[2]), .B(xor_1_out[2]), .Carry_IN(twobitadder_2_carry_out), .Sum(out_4[2]),
    .Carry_OUT(twobitadder_3_carry_out));
  TwoBitAdder twobitadder_4 (
    .A(A[3]), .B(xor_1_out[3]), .Carry_IN(twobitadder_3_carry_out), .Sum(out_4[3]),
    .Carry_OUT(twobitadder_4_carry_out));
  TwoBitAdder twobitadder_5 (
    .A(A[4]), .B(xor_1_out[4]), .Carry_IN(twobitadder_4_carry_out), .Sum(out_4[4]),
    .Carry_OUT(twobitadder_5_carry_out));
  TwoBitAdder twobitadder_6 (
    .A(A[5]), .B(xor_1_out[5]), .Carry_IN(twobitadder_5_carry_out), .Sum(out_4[5]),
    .Carry_OUT(twobitadder_6_carry_out));
  TwoBitAdder twobitadder_7 (
    .A(A[6]), .B(xor_1_out[6]), .Carry_IN(twobitadder_6_carry_out), .Sum(out_4[6]),
    .Carry_OUT(twobitadder_7_carry_out));
  TwoBitAdder twobitadder_8 (
    .A(A[7]), .B(xor_1_out[7]), .Carry_IN(twobitadder_7_carry_out), .Sum(out_4[7]),
    .Carry_OUT(twobitadder_8_carry_out));
  and and_1 (negativeoverflow, twobitadder_8_carry_out, xor_2_out);
  xor xor_2 (xor_2_out, twobitadder_8_carry_out, twobitadder_7_carry_out);
  and and_2 (positiveoverflow, xor_2_out, twobitadder_7_carry_out);
endmodule

module LeftShifter (
  input  [7:0] in_1,
  output [7:0] out_2,
  output Overflow
);


  assign out_2[7:1] = in_1[6:0];
  assign Overflow = in_1[7];
endmodule

module RightShifter (
  input  [7:0] in_1,
  output Underflow,
  output [7:0] out_3
);


  assign out_3[6:0] = in_1[7:1];
  assign Underflow = in_1[0];
endmodule

module CU2 (
  input  [3:0] OPCODE,
  input  [3:0] STEPCOUNTER,
  output MAR1OE,
  output RAMOE,
  output AWE,
  output MAR2OE,
  output BWE,
  output OUTWE,
  output FLAGWE,
  output OUTOE
);

  wire not_1_out, not_2_out, not_3_out, not_4_out, not_5_out, or_1_out, or_2_out, or_3_out, or_4_out,
       or_5_out, or_6_out, or_7_out, or_8_out, or_9_out, or_10_out, or_11_out, or_12_out, or_13_out;

  not not_1 (not_1_out, OPCODE[2]);
  not not_2 (not_2_out, STEPCOUNTER[3]);
  not not_3 (not_3_out, STEPCOUNTER[2]);
  not not_4 (not_4_out, STEPCOUNTER[1]);
  not not_5 (not_5_out, STEPCOUNTER[0]);
  or or_1 (or_1_out, OPCODE[3], not_1_out);
  or or_2 (or_2_out, OPCODE[3], not_1_out);
  or or_3 (or_3_out, OPCODE[3], not_1_out);
  or or_4 (or_4_out, OPCODE[3], not_1_out);
  or or_5 (or_5_out, OPCODE[3], not_1_out);
  or or_6 (or_6_out, STEPCOUNTER[3], STEPCOUNTER[2]);
  or or_7 (or_7_out, STEPCOUNTER[3], STEPCOUNTER[1]);
  or or_8 (or_8_out, STEPCOUNTER[2], not_4_out);
  or or_9 (or_9_out, not_3_out, STEPCOUNTER[1]);
  or or_10 (or_10_out, not_2_out, not_4_out);
  or or_11 (or_11_out, OPCODE[3], not_1_out);
  or or_12 (or_12_out, OPCODE[3], not_1_out);
  or or_13 (or_13_out, OPCODE[3], not_1_out);
  and and_1 (MAR1OE, STEPCOUNTER[2], not_5_out, not_4_out, not_2_out, or_1_out);
  and and_2 (RAMOE, STEPCOUNTER[2], not_5_out, not_2_out, or_2_out);
  and and_3 (AWE, STEPCOUNTER[2], STEPCOUNTER[0], not_4_out, not_2_out, or_3_out);
  and and_4 (MAR2OE, STEPCOUNTER[2], STEPCOUNTER[1], not_5_out, not_2_out, or_4_out);
  and and_5 (BWE, STEPCOUNTER[0], or_5_out, or_6_out, or_7_out, or_8_out, or_9_out, or_10_out);
  and and_6 (OUTWE, STEPCOUNTER[3], not_5_out, not_4_out, not_3_out, or_11_out);
  and and_7 (FLAGWE, STEPCOUNTER[3], not_5_out, not_4_out, not_3_out, or_12_out);
  and and_8 (OUTOE, STEPCOUNTER[3], STEPCOUNTER[0], not_4_out, not_3_out, or_13_out);
endmodule

module CU3 (
  input  [3:0] opcode,
  input  [3:0] stepcounter,
  output MAR1OE,
  output RAMOE,
  output BWE,
  output BOE,
  output RAMWE,
  output AWE,
  output RESET
);

  wire and_4_out, and_5_out, and_8_out, not_1_out, not_2_out, not_3_out, not_4_out, not_5_out, not_6_out;

  not not_1 (not_1_out, opcode[3]);
  not not_2 (not_2_out, opcode[1]);
  not not_3 (not_3_out, opcode[0]);
  not not_4 (not_4_out, stepcounter[3]);
  not not_5 (not_5_out, stepcounter[1]);
  not not_6 (not_6_out, stepcounter[0]);
  and and_1 (MAR1OE, not_1_out, opcode[2], not_2_out, not_4_out, stepcounter[2], not_5_out, not_6_out);
  and and_2 (RAMOE, not_1_out, opcode[2], not_2_out, not_3_out, not_4_out, stepcounter[2], not_5_out, not_6_out);
  and and_3 (BWE, not_1_out, opcode[2], not_2_out, not_3_out, not_4_out, stepcounter[2], not_5_out, stepcounter[0]);
  and and_4 (and_4_out, not_1_out, opcode[2], not_2_out, opcode[0], not_4_out, stepcounter[2], not_5_out, not_6_out);
  and and_5 (and_5_out, not_1_out, opcode[2], opcode[1], not_3_out, not_4_out, stepcounter[2], not_5_out, not_6_out);
  and and_6 (RAMWE, not_1_out, opcode[2], not_2_out, opcode[0], not_4_out, stepcounter[2], not_5_out, not_6_out);
  and and_7 (AWE, not_1_out, opcode[2], opcode[1], not_3_out, not_4_out, stepcounter[2], not_5_out, not_6_out);
  and and_8 (and_8_out, stepcounter[2], stepcounter[1]);
  or or_1 (BOE, and_4_out, and_5_out);
  and and_9 (RESET, and_8_out, not_1_out, opcode[2]);
endmodule
